# Fritzing sketch pcb (saved by Fritzing 0.9.3b)
circuit board: 1.9144cm x 6.06017cm
breadboards: 1

parts:
  R1 = Resistor [tolerance=±5% resistance=470 package="0805 [SMD]"]
  R2 = Resistor [tolerance=±5% resistance=470 package="0805 [SMD]"]
  R3 = Resistor [tolerance=±5% resistance=470 package="0805 [SMD]"]
  Q3 = MOSFET-NCHANNEL [package=dpak]
  Q2 = MOSFET-NCHANNEL [package=dpak]
  DC_in = Screw terminal - 2 pins [package=THT]
  RGB_out = screw terminal, 4 pins
  Arduino = Arduino Nano (Rev3.0)
  Q1 = MOSFET-NCHANNEL [package=dpak]

nets:
  N1: R1.Pin_0, Arduino.D6
  N2: R1.Pin_1, Q1.G
  N3: R2.Pin_0, Arduino.D5
  N4: R2.Pin_1, Q2.G
  N5: R3.Pin_0, Arduino.D3
  N6: R3.Pin_1, Q3.G
  N7: Q3.S, Q2.S, DC_in.pin2, Arduino.GND, Q1.S
  N8: Q3.D, RGB_out.pin3
  N9: Q2.D, RGB_out.pin2
  N10: DC_in.pin1, RGB_out.pin4
  N11: RGB_out.pin1, Q1.D

notes:
  +
  BRG+
  -+
  USB
